// Logisim project lab1_part2_q1.circ as structural Verilog: 1 circuit, main circuit main
module main (
  input  A,
  input  B,
  input  C,
  output F
);

  wire and_1_out, not_1_out, not_2_out, or_1_out;

  not not_1 (not_1_out, B);
  or or_1 (or_1_out, A, B);
  and and_1 (and_1_out, not_1_out, C);
  not not_2 (not_2_out, or_1_out);
  or or_2 (F, not_2_out, and_1_out);
endmodule
