// Logisim project lab1_part2_q3.circ as structural Verilog: 1 circuit, main circuit main
module main (
  input  B,
  input  A,
  input  C,
  output F
);

  wire not_1_out, not_2_out, or_1_out;

  not not_1 (not_1_out, B);
  not not_2 (not_2_out, A);
  or or_1 (or_1_out, not_2_out, C);
  and and_1 (F, not_1_out, or_1_out);
endmodule
