// Logisim project lab2_7_segment_decoder.circ as structural Verilog: 8 circuits, main circuit main
module main (
  input  SW_2,
  input  SW_3,
  input  SW_0,
  input  SW_1
);

  wire seg0_m, seg1_m, seg2_m, seg3_m, seg4_m, seg5_m, seg6_m;

  segment0 seg0 (.c0(SW_0), .c2(SW_2), .c1(SW_1), .c3(SW_3), .m(seg0_m));
  segment1 seg1 (.c0(SW_0), .c1(SW_1), .c2(SW_2), .c3(SW_3), .m(seg1_m));
  segment2 seg2 (.c3(SW_3), .c2(SW_2), .c0(SW_0), .c1(SW_1), .m(seg2_m));
  segment3 seg3 (.c3(SW_3), .c2(SW_2), .c1(SW_1), .c0(SW_0), .m(seg3_m));
  segment4 seg4 (.c3(SW_3), .c1(SW_1), .c2(SW_2), .c0(SW_0), .m(seg4_m));
  segment5 seg5 (.c2(SW_2), .c3(SW_3), .c1(SW_1), .c0(SW_0), .m(seg5_m));
  segment6 seg6 (.c1(SW_1), .c0(SW_0), .c3(SW_3), .c2(SW_2), .m(seg6_m));
  _7_Segment_Display HEX (
    .g(seg6_m), .f(seg5_m), .a(seg0_m), .b(seg1_m), .e(seg4_m), .d(seg3_m), .c(seg2_m));  // open: dp
endmodule

module segment0 (
  input  c0,
  input  c2,
  input  c1,
  input  c3,
  output m
);

  wire and_1_out, and_2_out, and_3_out, and_4_out, and_5_out, nor_1_out, not_1_out, not_2_out, not_3_out,
       not_4_out, not_5_out;

  not not_1 (not_1_out, c0);
  not not_2 (not_2_out, c3);
  not not_3 (not_3_out, c2);
  not not_4 (not_4_out, c1);
  not not_5 (not_5_out, c3);
  and and_1 (and_1_out, not_1_out, c3);
  and and_2 (and_2_out, c2, c1);
  and and_3 (and_3_out, c1, not_2_out);
  and and_4 (and_4_out, c3, not_3_out, not_4_out);
  nor nor_1 (nor_1_out, c0, c2, c3);
  and and_5 (and_5_out, c2, c0, not_5_out);
  or or_1 (m, and_1_out, and_2_out, and_3_out, and_4_out, nor_1_out, and_5_out);
endmodule

module segment1 (
  input  c0,
  input  c1,
  input  c2,
  input  c3,
  output m
);

  wire and_1_out, and_2_out, and_3_out, nor_1_out, nor_2_out, nor_3_out, not_1_out, not_2_out, not_3_out,
       not_4_out;

  not not_1 (not_1_out, c3);
  not not_2 (not_2_out, c0);
  not not_3 (not_3_out, c2);
  nor nor_1 (nor_1_out, c2, c3);
  not not_4 (not_4_out, c1);
  and and_1 (and_1_out, not_4_out, c3, c0);
  and and_2 (and_2_out, c1, not_1_out, c0);
  and and_3 (and_3_out, c1, not_2_out, not_3_out);
  nor nor_2 (nor_2_out, c0, c3, c1);
  nor nor_3 (nor_3_out, c1, c2);
  or or_1 (m, nor_2_out, nor_3_out, nor_1_out, and_1_out, and_2_out, and_3_out);
endmodule

module segment2 (
  input  c3,
  input  c2,
  input  c0,
  input  c1,
  output m
);

  wire and_1_out, and_2_out, and_3_out, and_4_out, nor_1_out, not_1_out, not_2_out, not_3_out;

  not not_1 (not_1_out, c2);
  not not_2 (not_2_out, c3);
  and and_1 (and_1_out, not_1_out, c3);
  and and_2 (and_2_out, not_2_out, c2);
  and and_3 (and_3_out, not_2_out, not_1_out, c0);
  not not_3 (not_3_out, c1);
  nor nor_1 (nor_1_out, c2, c1);
  and and_4 (and_4_out, c2, c0, not_3_out);
  or or_1 (m, and_1_out, and_2_out, and_3_out, and_4_out, nor_1_out);
endmodule

module segment3 (
  input  c3,
  input  c2,
  input  c1,
  input  c0,
  output m
);

  wire and_1_out, and_2_out, and_3_out, and_4_out, and_5_out, nor_1_out, not_1_out, not_2_out, not_3_out,
       not_4_out, not_5_out;

  not not_1 (not_1_out, c3);
  not not_2 (not_2_out, c0);
  not not_3 (not_3_out, c1);
  not not_4 (not_4_out, c0);
  not not_5 (not_5_out, c2);
  and and_1 (and_1_out, not_1_out, c1, not_2_out);
  and and_2 (and_2_out, c3, not_3_out, not_2_out);
  and and_3 (and_3_out, c2, not_3_out, c0);
  nor nor_1 (nor_1_out, c2, c1, c0);
  and and_4 (and_4_out, c2, not_4_out, c1);
  and and_5 (and_5_out, c1, c0, not_5_out);
  or or_1 (m, and_1_out, and_2_out, and_3_out, nor_1_out, and_4_out, and_5_out);
endmodule

module segment4 (
  input  c3,
  input  c1,
  input  c2,
  input  c0,
  output m
);

  wire and_1_out, and_2_out, and_3_out, and_4_out, nor_1_out, not_1_out, not_2_out, not_3_out;

  not not_1 (not_1_out, c3);
  not not_2 (not_2_out, c1);
  not not_3 (not_3_out, c0);
  and and_1 (and_1_out, c3, c1);
  and and_2 (and_2_out, c3, not_2_out, c2);
  and and_3 (and_3_out, not_2_out, not_3_out, c3);
  and and_4 (and_4_out, not_3_out, not_1_out, c1);
  nor nor_1 (nor_1_out, c3, c2, c0);
  or or_1 (m, and_1_out, and_2_out, and_3_out, and_4_out, nor_1_out);
endmodule

module segment5 (
  input  c2,
  input  c3,
  input  c1,
  input  c0,
  output m
);

  wire and_1_out, and_2_out, and_3_out, and_4_out, nor_1_out, not_1_out, not_2_out, not_3_out, not_4_out;

  not not_1 (not_1_out, c3);
  not not_2 (not_2_out, c1);
  not not_3 (not_3_out, c2);
  not not_4 (not_4_out, c0);
  and and_1 (and_1_out, c2, not_1_out, not_2_out);
  and and_2 (and_2_out, not_3_out, c3);
  and and_3 (and_3_out, c3, c1);
  nor nor_1 (nor_1_out, c1, c0);
  and and_4 (and_4_out, c2, c1, not_4_out);
  or or_1 (m, and_1_out, and_2_out, and_3_out, nor_1_out, and_4_out);
endmodule

module segment6 (
  input  c1,
  input  c0,
  input  c3,
  input  c2,
  output m
);

  wire and_1_out, and_2_out, and_3_out, and_4_out, and_5_out, not_1_out, not_2_out, not_3_out, not_4_out;

  not not_1 (not_1_out, c0);
  not not_2 (not_2_out, c1);
  not not_3 (not_3_out, c3);
  not not_4 (not_4_out, c2);
  and and_1 (and_1_out, c1, not_1_out);
  and and_2 (and_2_out, c0, c3);
  and and_3 (and_3_out, not_2_out, not_3_out, c2);
  and and_4 (and_4_out, not_3_out, not_4_out, c1);
  and and_5 (and_5_out, not_4_out, c3);
  or or_1 (m, and_1_out, and_2_out, and_3_out, and_4_out, and_5_out);
endmodule
