// Logisim project lab3_part1.circ as structural Verilog: 1 circuit, main circuit main
module main (
  input  [5:0] SW,
  input  [2:0] sel,
  output LEDR0
);

  Multiplexer #(.enable("false"), .select(3)) multiplexer_1 (
    .in0(SW[0]), .in1(SW[1]), .in2(SW[2]), .in3(SW[3]), .in4(SW[4]), .in5(SW[5]), .in6(1'b0), .in7(1'b0),
    .out(LEDR0), .sel(sel));
endmodule
