// Logisim project lab3_part2.circ as structural Verilog: 2 circuits, main circuit main
module main (
  input  c_in,
  input  [3:0] A,
  input  [3:0] B,
  output [3:0] S,
  output c_out
);

  wire fa_1_c_out, fa_2_c_out, fa_3_c_out;

  FA fa_1 (.c_in(c_in), .A(A[0]), .B(B[0]), .S(S[0]), .c_out(fa_1_c_out));
  FA fa_2 (.c_in(fa_1_c_out), .A(A[1]), .B(B[1]), .S(S[1]), .c_out(fa_2_c_out));
  FA fa_3 (.c_in(fa_2_c_out), .A(A[2]), .B(B[2]), .S(S[2]), .c_out(fa_3_c_out));
  FA fa_4 (.c_in(fa_3_c_out), .A(A[3]), .B(B[3]), .S(S[3]), .c_out(c_out));
endmodule

module FA (
  input  c_in,
  input  A,
  input  B,
  output S,
  output c_out
);

  wire xor_1_out;

  xor xor_1 (xor_1_out, A, B);
  Multiplexer #(.enable("false")) multiplexer_1 (.in0(B), .in1(c_in), .out(c_out), .sel(xor_1_out));
  xor xor_2 (S, c_in, xor_1_out);
endmodule
