// Logisim project lab4_part1.circ as structural Verilog: 2 circuits, main circuit gated_D_latch
module gated_D_latch (
  input  D,
  input  Clk,
  output Qa,
  output Qb
);

  wire nand_1_out, nand_2_out, not_1_out;

  not not_1 (not_1_out, D);
  nand nand_1 (nand_1_out, D, Clk);
  nand nand_2 (nand_2_out, Clk, not_1_out);
  nand nand_3 (Qa, nand_1_out, Qb);
  nand nand_4 (Qb, Qa, nand_2_out);
endmodule

module master_slave_flip_flop (
  input  D,
  input  Clk,
  output Q,
  output not_Q
);

  wire gated_d_latch_1_qa, not_1_out;

  not not_1 (not_1_out, Clk);
  gated_D_latch gated_d_latch_1 (.D(D), .Clk(Clk), .Qa(gated_d_latch_1_qa));  // open: Qb
  gated_D_latch gated_d_latch_2 (.D(gated_d_latch_1_qa), .Clk(not_1_out), .Qa(Q), .Qb(not_Q));
endmodule
