// Logisim project lab4_part2.circ as structural Verilog: 22 circuits, main circuit ALU
module ALU (
  input  [3:0] A,
  input  [2:0] func,
  input  Clk,
  input  reset,
  output [3:0] S1,
  output [3:0] S2
);

  wire [7:0] alu_component_1_s;

  ALU_component alu_component_1 (.A(A), .B(S2), .sel(func), .S(alu_component_1_s));
  Register register_1 (.D(alu_component_1_s), .clk(Clk), .Q({S1, S2}), .clr(reset));  // open: en
  Hex_Digit_Display hex_digit_display_1 (.value(S1));  // open: dp
  Hex_Digit_Display hex_digit_display_2 (.value(S2));  // open: dp
endmodule

module ALU_component (
  input  [3:0] A,
  input  [3:0] B,
  input  [2:0] sel,
  output [7:0] S
);

  wire func0_1_c_out, func1_1_c_out, func2_1_c_out, multiplexer_2_out;
  wire [4:4] multiplexer_1_out;
  wire [7:0] func0_1_s, func1_1_s, func2_1_s, func3_1_s, func4_1_s, func5_1_s, func6_1_s, func7_1_s;

  func0 func0_1 (.A(A), .S(func0_1_s), .c_out(func0_1_c_out));
  func1 func1_1 (.A(A), .B(B), .S(func1_1_s), .c_out(func1_1_c_out));
  func2 func2_1 (.A(A), .B(B), .S(func2_1_s), .c_out(func2_1_c_out));
  func3 func3_1 (.A(A), .B(B), .S(func3_1_s));
  func4 func4_1 (.A(A), .B(B), .S(func4_1_s));
  func5 func5_1 (.B(B), .A(A), .S(func5_1_s));
  func6 func6_1 (.B(B), .A(A), .S(func6_1_s));
  func7 func7_1 (.A(A), .B(B), .S(func7_1_s));
  Multiplexer #(.enable("false"), .select(3), .width(8)) multiplexer_1 (
    .in0(func0_1_s), .in1(func1_1_s), .in2(func2_1_s), .in3(func3_1_s), .in4(func4_1_s), .in5(func5_1_s),
    .in6(func6_1_s), .in7(func7_1_s), .out({S[7:5], multiplexer_1_out[4], S[3:0]}), .sel(sel));
  Multiplexer #(.enable("false"), .select(3)) multiplexer_2 (
    .in0(func0_1_c_out), .in1(func1_1_c_out), .in2(func2_1_c_out), .in3(1'b0), .in4(1'b0), .in5(1'b0),
    .in6(1'b0), .in7(1'b0), .out(multiplexer_2_out), .sel(sel));
  or or_1 (S[4], multiplexer_2_out, multiplexer_1_out[4]);
endmodule

module lab3_ALU (
  input  [3:0] A,
  input  [3:0] B,
  input  [2:0] sel,
  output c_out,
  output [7:0] S
);

  wire func0_1_c_out, func1_1_c_out, func2_1_c_out, or_1_out, seven_seg_decoder_1_d0, seven_seg_decoder_1_d1,
       seven_seg_decoder_1_d2, seven_seg_decoder_1_u0, seven_seg_decoder_1_u1, seven_seg_decoder_1_u2,
       seven_seg_decoder_1_u3, seven_seg_decoder_2_d0, seven_seg_decoder_2_d1, seven_seg_decoder_2_d2,
       seven_seg_decoder_2_u0, seven_seg_decoder_2_u1, seven_seg_decoder_2_u2, seven_seg_decoder_2_u3;
  wire [7:0] func0_1_s, func1_1_s, func2_1_s, func3_1_s, func4_1_s, func5_1_s;

  Hex_Digit_Display hex_digit_display_1 (.value(A));  // open: dp
  Hex_Digit_Display hex_digit_display_2 (.value(B));  // open: dp
  func0 func0_1 (.A(A), .S(func0_1_s), .c_out(func0_1_c_out));
  func1 func1_1 (.A(A), .B(B), .S(func1_1_s), .c_out(func1_1_c_out));
  func2 func2_1 (.A(A), .B(B), .S(func2_1_s), .c_out(func2_1_c_out));
  func3 func3_1 (.A(A), .B(B), .S(func3_1_s));
  func4 func4_1 (.A(A), .B(B), .S(func4_1_s));
  func5 func5_1 (.B(B), .A(A), .S(func5_1_s));
  Multiplexer #(.enable("false"), .select(3), .width(8)) multiplexer_1 (
    .in0(func0_1_s), .in1(func1_1_s), .in2(func2_1_s), .in3(func3_1_s), .in4(func4_1_s), .in5(func5_1_s),
    .in6({8{1'b0}}), .in7({8{1'b0}}), .out(S), .sel(sel));
  Multiplexer #(.enable("false"), .select(3)) multiplexer_2 (
    .in0(func0_1_c_out), .in1(func1_1_c_out), .in2(func2_1_c_out), .out(c_out), .sel(sel));  // open: in3, in4, in5, in6, in7
  LED led_1 (.in(S[5]));
  LED led_2 (.in(or_1_out));
  _7_Segment_Display u_7_segment_display_1 (
    .g(seven_seg_decoder_1_u0), .f(seven_seg_decoder_1_u1), .a(seven_seg_decoder_1_u2),
    .b(seven_seg_decoder_1_u3), .e(seven_seg_decoder_1_d0), .d(seven_seg_decoder_1_d1),
    .c(seven_seg_decoder_1_d2));  // open: dp
  or or_1 (or_1_out, c_out, S[4]);
  LED led_3 (.in(S[7]));
  LED led_4 (.in(S[6]));
  seven_seg_decoder seven_seg_decoder_1 (
    .SW_2(S[6]), .SW_3(S[7]), .SW_0(or_1_out), .SW_1(S[5]), .u2(seven_seg_decoder_1_u2),
    .u3(seven_seg_decoder_1_u3), .d2(seven_seg_decoder_1_d2), .d1(seven_seg_decoder_1_d1),
    .d0(seven_seg_decoder_1_d0), .u1(seven_seg_decoder_1_u1), .u0(seven_seg_decoder_1_u0));
  _7_Segment_Display u_7_segment_display_2 (
    .g(seven_seg_decoder_2_u0), .f(seven_seg_decoder_2_u1), .a(seven_seg_decoder_2_u2),
    .b(seven_seg_decoder_2_u3), .e(seven_seg_decoder_2_d0), .d(seven_seg_decoder_2_d1),
    .c(seven_seg_decoder_2_d2));  // open: dp
  LED led_5 (.in(S[1]));
  LED led_6 (.in(S[0]));
  LED led_7 (.in(S[3]));
  LED led_8 (.in(S[2]));
  seven_seg_decoder seven_seg_decoder_2 (
    .SW_2(S[2]), .SW_3(S[3]), .SW_0(S[0]), .SW_1(S[1]), .u2(seven_seg_decoder_2_u2),
    .u3(seven_seg_decoder_2_u3), .d2(seven_seg_decoder_2_d2), .d1(seven_seg_decoder_2_d1),
    .d0(seven_seg_decoder_2_d0), .u1(seven_seg_decoder_2_u1), .u0(seven_seg_decoder_2_u0));
endmodule

module seven_seg_decoder (
  input  SW_2,
  input  SW_3,
  input  SW_0,
  input  SW_1,
  output u2,
  output u3,
  output d2,
  output d1,
  output d0,
  output u1,
  output u0
);

  segment0 seg0 (.c0(SW_0), .c2(SW_2), .c1(SW_1), .c3(SW_3), .m(u2));
  segment1 seg1 (.c0(SW_0), .c1(SW_1), .c2(SW_2), .c3(SW_3), .m(u3));
  segment2 seg2 (.c3(SW_3), .c2(SW_2), .c0(SW_0), .c1(SW_1), .m(d2));
  segment3 seg3 (.c3(SW_3), .c2(SW_2), .c1(SW_1), .c0(SW_0), .m(d1));
  segment4 seg4 (.c3(SW_3), .c1(SW_1), .c2(SW_2), .c0(SW_0), .m(d0));
  segment5 seg5 (.c2(SW_2), .c3(SW_3), .c1(SW_1), .c0(SW_0), .m(u1));
  segment6 seg6 (.c1(SW_1), .c0(SW_0), .c3(SW_3), .c2(SW_2), .m(u0));
endmodule

module segment0 (
  input  c0,
  input  c2,
  input  c1,
  input  c3,
  output m
);

  wire and_1_out, and_2_out, and_3_out, and_4_out, and_5_out, nor_1_out, not_1_out, not_2_out, not_3_out,
       not_4_out, not_5_out;

  not not_1 (not_1_out, c0);
  not not_2 (not_2_out, c3);
  not not_3 (not_3_out, c2);
  not not_4 (not_4_out, c1);
  not not_5 (not_5_out, c3);
  and and_1 (and_1_out, not_1_out, c3);
  and and_2 (and_2_out, c2, c1);
  and and_3 (and_3_out, c1, not_2_out);
  and and_4 (and_4_out, c3, not_3_out, not_4_out);
  nor nor_1 (nor_1_out, c0, c2, c3);
  and and_5 (and_5_out, c2, c0, not_5_out);
  or or_1 (m, and_1_out, and_2_out, and_3_out, and_4_out, nor_1_out, and_5_out);
endmodule

module segment1 (
  input  c0,
  input  c1,
  input  c2,
  input  c3,
  output m
);

  wire and_1_out, and_2_out, and_3_out, nor_1_out, nor_2_out, nor_3_out, not_1_out, not_2_out, not_3_out,
       not_4_out;

  not not_1 (not_1_out, c3);
  not not_2 (not_2_out, c0);
  not not_3 (not_3_out, c2);
  nor nor_1 (nor_1_out, c2, c3);
  not not_4 (not_4_out, c1);
  and and_1 (and_1_out, not_4_out, c3, c0);
  and and_2 (and_2_out, c1, not_1_out, c0);
  and and_3 (and_3_out, c1, not_2_out, not_3_out);
  nor nor_2 (nor_2_out, c0, c3, c1);
  nor nor_3 (nor_3_out, c1, c2);
  or or_1 (m, nor_2_out, nor_3_out, nor_1_out, and_1_out, and_2_out, and_3_out);
endmodule

module segment2 (
  input  c3,
  input  c2,
  input  c0,
  input  c1,
  output m
);

  wire and_1_out, and_2_out, and_3_out, and_4_out, nor_1_out, not_1_out, not_2_out, not_3_out;

  not not_1 (not_1_out, c2);
  not not_2 (not_2_out, c3);
  and and_1 (and_1_out, not_1_out, c3);
  and and_2 (and_2_out, not_2_out, c2);
  and and_3 (and_3_out, not_2_out, not_1_out, c0);
  not not_3 (not_3_out, c1);
  nor nor_1 (nor_1_out, c2, c1);
  and and_4 (and_4_out, c2, c0, not_3_out);
  or or_1 (m, and_1_out, and_2_out, and_3_out, and_4_out, nor_1_out);
endmodule

module segment3 (
  input  c3,
  input  c2,
  input  c1,
  input  c0,
  output m
);

  wire and_1_out, and_2_out, and_3_out, and_4_out, and_5_out, nor_1_out, not_1_out, not_2_out, not_3_out,
       not_4_out, not_5_out;

  not not_1 (not_1_out, c3);
  not not_2 (not_2_out, c0);
  not not_3 (not_3_out, c1);
  not not_4 (not_4_out, c0);
  not not_5 (not_5_out, c2);
  and and_1 (and_1_out, not_1_out, c1, not_2_out);
  and and_2 (and_2_out, c3, not_3_out, not_2_out);
  and and_3 (and_3_out, c2, not_3_out, c0);
  nor nor_1 (nor_1_out, c2, c1, c0);
  and and_4 (and_4_out, c2, not_4_out, c1);
  and and_5 (and_5_out, c1, c0, not_5_out);
  or or_1 (m, and_1_out, and_2_out, and_3_out, nor_1_out, and_4_out, and_5_out);
endmodule

module segment4 (
  input  c3,
  input  c1,
  input  c2,
  input  c0,
  output m
);

  wire and_1_out, and_2_out, and_3_out, and_4_out, nor_1_out, not_1_out, not_2_out, not_3_out;

  not not_1 (not_1_out, c3);
  not not_2 (not_2_out, c1);
  not not_3 (not_3_out, c0);
  and and_1 (and_1_out, c3, c1);
  and and_2 (and_2_out, c3, not_2_out, c2);
  and and_3 (and_3_out, not_2_out, not_3_out, c3);
  and and_4 (and_4_out, not_3_out, not_1_out, c1);
  nor nor_1 (nor_1_out, c3, c2, c0);
  or or_1 (m, and_1_out, and_2_out, and_3_out, and_4_out, nor_1_out);
endmodule

module segment5 (
  input  c2,
  input  c3,
  input  c1,
  input  c0,
  output m
);

  wire and_1_out, and_2_out, and_3_out, and_4_out, nor_1_out, not_1_out, not_2_out, not_3_out, not_4_out;

  not not_1 (not_1_out, c3);
  not not_2 (not_2_out, c1);
  not not_3 (not_3_out, c2);
  not not_4 (not_4_out, c0);
  and and_1 (and_1_out, c2, not_1_out, not_2_out);
  and and_2 (and_2_out, not_3_out, c3);
  and and_3 (and_3_out, c3, c1);
  nor nor_1 (nor_1_out, c1, c0);
  and and_4 (and_4_out, c2, c1, not_4_out);
  or or_1 (m, and_1_out, and_2_out, and_3_out, nor_1_out, and_4_out);
endmodule

module segment6 (
  input  c1,
  input  c0,
  input  c3,
  input  c2,
  output m
);

  wire and_1_out, and_2_out, and_3_out, and_4_out, and_5_out, not_1_out, not_2_out, not_3_out, not_4_out;

  not not_1 (not_1_out, c0);
  not not_2 (not_2_out, c1);
  not not_3 (not_3_out, c3);
  not not_4 (not_4_out, c2);
  and and_1 (and_1_out, c1, not_1_out);
  and and_2 (and_2_out, c0, c3);
  and and_3 (and_3_out, not_2_out, not_3_out, c2);
  and and_4 (and_4_out, not_3_out, not_4_out, c1);
  and and_5 (and_5_out, not_4_out, c3);
  or or_1 (m, and_1_out, and_2_out, and_3_out, and_4_out, and_5_out);
endmodule

module FA (
  input  c_in,
  input  A,
  input  B,
  output S,
  output c_out
);

  wire xor_1_out;

  xor xor_1 (xor_1_out, A, B);
  Multiplexer #(.enable("false")) multiplexer_1 (.in0(B), .in1(c_in), .out(c_out), .sel(xor_1_out));
  xor xor_2 (S, c_in, xor_1_out);
endmodule

module func0 (
  input  [3:0] A,
  output [7:0] S,
  output c_out
);

  wire fa_1_c_out, fa_2_c_out, fa_3_c_out;
  wire [3:0] fa_1_s;

  FA fa_1 (.c_in(1'b0), .A(A[0]), .B(1'b1), .S(fa_1_s[0]), .c_out(fa_1_c_out));
  FA fa_2 (.c_in(fa_1_c_out), .A(A[1]), .B(1'b0), .S(fa_1_s[1]), .c_out(fa_2_c_out));
  FA fa_3 (.c_in(fa_2_c_out), .A(A[2]), .B(1'b0), .S(fa_1_s[2]), .c_out(fa_3_c_out));
  FA fa_4 (.c_in(fa_3_c_out), .A(A[3]), .B(1'b0), .S(fa_1_s[3]), .c_out(c_out));
  assign S = {{4{1'b0}}, fa_1_s};  // Bit_Extender bit_extender_1
endmodule

module func1 (
  input  [3:0] A,
  input  [3:0] B,
  output [7:0] S,
  output c_out
);

  wire fa_1_c_out, fa_2_c_out, fa_3_c_out;
  wire [3:0] fa_1_s;

  FA fa_1 (.c_in(1'b0), .A(A[0]), .B(B[0]), .S(fa_1_s[0]), .c_out(fa_1_c_out));
  FA fa_2 (.c_in(fa_1_c_out), .A(A[1]), .B(B[1]), .S(fa_1_s[1]), .c_out(fa_2_c_out));
  FA fa_3 (.c_in(fa_2_c_out), .A(A[2]), .B(B[2]), .S(fa_1_s[2]), .c_out(fa_3_c_out));
  FA fa_4 (.c_in(fa_3_c_out), .A(A[3]), .B(B[3]), .S(fa_1_s[3]), .c_out(c_out));
  assign S = {{4{1'b0}}, fa_1_s};  // Bit_Extender bit_extender_1
endmodule

module func2 (
  input  [3:0] A,
  input  [3:0] B,
  output [7:0] S,
  output c_out
);

  wire [3:0] adder_1_out;

  Adder #(.width(4)) adder_1 (.a(A), .b(B), .out(adder_1_out), .cin(1'b0), .cout(c_out));
  assign S = {{4{1'b0}}, adder_1_out};  // Bit_Extender bit_extender_1
endmodule

module func3 (
  input  [3:0] A,
  input  [3:0] B,
  output [7:0] S
);

  fourbitOR fourbitor_1 (.A(A), .B(B), .S(S[3:0]));
  fourbitXOR fourbitxor_1 (.A(A), .B(B), .S(S[7:4]));
endmodule

module func4 (
  input  [3:0] A,
  input  [3:0] B,
  output [7:0] S
);

  wire or_1_out, or_2_out, or_3_out, or_4_out, or_5_out;

  or or_1 (or_1_out, A[0], B[0]);
  or or_2 (or_2_out, A[1], B[1]);
  or or_3 (or_3_out, A[2], B[2]);
  or or_4 (or_4_out, A[3], B[3]);
  assign S = {{7{1'b0}}, or_5_out};  // Bit_Extender bit_extender_1
  or or_5 (or_5_out, or_1_out, or_2_out, or_3_out, or_4_out);
endmodule

module func5 (
  input  [3:0] B,
  input  [3:0] A,
  output [7:0] S
);

  wire [8:0] bit_extender_1_out, shifter_1_out;

  assign bit_extender_1_out = {{5{1'b0}}, B};  // Bit_Extender bit_extender_1
  Shifter #(.width(9)) shifter_1 (.in(bit_extender_1_out), .\dist (A), .out(shifter_1_out));
  Bit_Extender #(.in_width(9), .out_width(8), .\type ("zero")) bit_extender_2 (.in(shifter_1_out), .out(S));
endmodule

module func6 (
  input  [3:0] B,
  input  [3:0] A,
  output [7:0] S
);

  wire [8:0] bit_extender_1_out, shifter_1_out;

  assign bit_extender_1_out = {{5{1'b0}}, B};  // Bit_Extender bit_extender_1
  Shifter #(.shift("lr"), .width(9)) shifter_1 (.in(bit_extender_1_out), .\dist (A), .out(shifter_1_out));
  Bit_Extender #(.in_width(9), .out_width(8), .\type ("zero")) bit_extender_2 (.in(shifter_1_out), .out(S));
endmodule

module func7 (
  input  [3:0] A,
  input  [3:0] B,
  output [7:0] S
);

  Multiplier #(.width(4)) multiplier_1 (.a(A), .b(B), .out(S[3:0]), .cout(S[7:4]));  // open: cin
endmodule

module fourbitOR (
  input  [3:0] A,
  input  [3:0] B,
  output [3:0] S
);

  or or_1 (S[0], A[0], B[0]);
  or or_2 (S[1], A[1], B[1]);
  or or_3 (S[2], A[2], B[2]);
  or or_4 (S[3], A[3], B[3]);
endmodule

module fourbitXOR (
  input  [3:0] A,
  input  [3:0] B,
  output [3:0] S
);

  xor xor_1 (S[0], A[0], B[0]);
  xor xor_2 (S[1], A[1], B[1]);
  xor xor_3 (S[2], A[2], B[2]);
  xor xor_4 (S[3], A[3], B[3]);
endmodule
