// Logisim project lab4_part3.circ as structural Verilog: 3 circuits, main circuit simplified_shifter
module simplified_shifter (
  input  ASR,
  input  [7:0] load_val,
  input  Clk,
  input  ShiftRight,
  input  reset,
  input  load_n,
  output [7:0] Q
);

  eight_bit_shift_register eight_bit_shift_register_1 (
    .ASR(ASR), .load_val(load_val), .Clk(Clk), .ShiftRight(ShiftRight), .reset(reset), .load_n(load_n), .Q(Q));
endmodule

module single_bit_shift_register (
  input  load_val,
  input  D_in,
  input  Clk,
  input  shift,
  input  load_n,
  input  reset,
  output Q_out
);

  wire multiplexer_1_out, multiplexer_2_out;

  Multiplexer #(.enable("false")) multiplexer_1 (.in0(Q_out), .in1(D_in), .out(multiplexer_1_out), .sel(shift));
  Multiplexer #(.enable("false")) multiplexer_2 (
    .in0(load_val), .in1(multiplexer_1_out), .out(multiplexer_2_out), .sel(load_n));
  D_Flip_Flop d_ff_1 (.D(multiplexer_2_out), .clk(Clk), .Q(Q_out), .reset(reset));  // open: Qn, preset
endmodule

module eight_bit_shift_register (
  input  ASR,
  input  [7:0] load_val,
  input  Clk,
  input  ShiftRight,
  input  reset,
  input  load_n,
  output [7:0] Q
);

  wire and_1_out;

  single_bit_shift_register single_bit_shift_register_1 (
    .load_val(load_val[0]), .D_in(Q[1]), .Clk(Clk), .shift(ShiftRight), .load_n(load_n), .reset(reset),
    .Q_out(Q[0]));
  single_bit_shift_register single_bit_shift_register_2 (
    .load_val(load_val[1]), .D_in(Q[2]), .Clk(Clk), .shift(ShiftRight), .load_n(load_n), .reset(reset),
    .Q_out(Q[1]));
  single_bit_shift_register single_bit_shift_register_3 (
    .load_val(load_val[2]), .D_in(Q[3]), .Clk(Clk), .shift(ShiftRight), .load_n(load_n), .reset(reset),
    .Q_out(Q[2]));
  single_bit_shift_register single_bit_shift_register_4 (
    .load_val(load_val[3]), .D_in(Q[4]), .Clk(Clk), .shift(ShiftRight), .load_n(load_n), .reset(reset),
    .Q_out(Q[3]));
  single_bit_shift_register single_bit_shift_register_5 (
    .load_val(load_val[4]), .D_in(Q[5]), .Clk(Clk), .shift(ShiftRight), .load_n(load_n), .reset(reset),
    .Q_out(Q[4]));
  single_bit_shift_register single_bit_shift_register_6 (
    .load_val(load_val[5]), .D_in(Q[6]), .Clk(Clk), .shift(ShiftRight), .load_n(load_n), .reset(reset),
    .Q_out(Q[5]));
  single_bit_shift_register single_bit_shift_register_7 (
    .load_val(load_val[6]), .D_in(Q[7]), .Clk(Clk), .shift(ShiftRight), .load_n(load_n), .reset(reset),
    .Q_out(Q[6]));
  single_bit_shift_register single_bit_shift_register_8 (
    .load_val(load_val[7]), .D_in(and_1_out), .Clk(Clk), .shift(ShiftRight), .load_n(load_n), .reset(reset),
    .Q_out(Q[7]));
  and and_1 (and_1_out, ASR, Q[7]);
endmodule
