// Logisim project lab5_part1.circ as structural Verilog: 1 circuit, main circuit main
module main (
  input  EN,
  input  clk,
  input  Clear_b,
  output [7:0] out_4
);

  wire and_1_out, and_2_out, and_3_out, and_4_out, and_5_out, and_6_out, and_7_out, not_1_out;

  T_Flip_Flop t_ff_1 (.T(EN), .clk(clk), .Q(out_4[0]), .reset(not_1_out));  // open: Qn, preset
  not not_1 (not_1_out, Clear_b);
  and and_1 (and_1_out, EN, out_4[0]);
  T_Flip_Flop t_ff_2 (.T(and_1_out), .clk(clk), .Q(out_4[1]), .reset(not_1_out));  // open: Qn, preset
  and and_2 (and_2_out, and_1_out, out_4[1]);
  T_Flip_Flop t_ff_3 (.T(and_2_out), .clk(clk), .Q(out_4[2]), .reset(not_1_out));  // open: Qn, preset
  and and_3 (and_3_out, and_2_out, out_4[2]);
  T_Flip_Flop t_ff_4 (.T(and_3_out), .clk(clk), .Q(out_4[3]), .reset(not_1_out));  // open: Qn, preset
  and and_4 (and_4_out, and_3_out, out_4[3]);
  T_Flip_Flop t_ff_5 (.T(and_4_out), .clk(clk), .Q(out_4[4]), .reset(not_1_out));  // open: Qn, preset
  and and_5 (and_5_out, and_4_out, out_4[4]);
  T_Flip_Flop t_ff_6 (.T(and_5_out), .clk(clk), .Q(out_4[5]), .reset(not_1_out));  // open: Qn, preset
  and and_6 (and_6_out, and_5_out, out_4[5]);
  T_Flip_Flop t_ff_7 (.T(and_6_out), .clk(clk), .Q(out_4[6]), .reset(not_1_out));  // open: Qn, preset
  and and_7 (and_7_out, and_6_out, out_4[6]);
  T_Flip_Flop t_ff_8 (.T(and_7_out), .clk(clk), .Q(out_4[7]), .reset(not_1_out));  // open: Qn, preset
  Hex_Digit_Display hex_digit_display_1 (.value(out_4[7:4]));  // open: dp
  Hex_Digit_Display hex_digit_display_2 (.value(out_4[3:0]));  // open: dp
endmodule
