// Logisim project lab5_part2.circ as structural Verilog: 6 circuits, main circuit DisplayCounter
module main (
  input  SW0,
  input  SW1,
  input  reset
);

  wire clk_out, ratedivider_1_output_clk;
  wire [3:0] displaycounter_1_q;

  Clock clk (.out(clk_out));
  RateDivider ratedivider_1 (.clk(clk_out), .SW0(SW0), .SW1(SW1), .reset(reset), .output_clk(ratedivider_1_output_clk));
  Hex_Digit_Display HEX0 (.value(displaycounter_1_q));  // open: dp
  DisplayCounter displaycounter_1 (
    .clear(reset), .clk(ratedivider_1_output_clk), .Enable(1'b1), .Q(displaycounter_1_q));

  // Notes on the sheet:
  //   HEX0
endmodule

module RateDivider (
  input  clk,
  input  SW0,
  input  SW1,
  input  reset,
  output output_clk
);

  wire and_1_out, and_2_out, and_3_out, and_4_out, nor_1_out, not_1_out, not_2_out, rd_1hz_1_output_clk,
       rd_05hz_1_output_clk, rd_025hz_1_output_clk;

  nor nor_1 (nor_1_out, SW0, SW1);
  and and_1 (and_1_out, clk, nor_1_out);
  and and_2 (and_2_out, SW0, not_1_out);
  not not_1 (not_1_out, SW1);
  not not_2 (not_2_out, SW0);
  and and_3 (and_3_out, not_2_out, SW1);
  and and_4 (and_4_out, SW0, SW1);
  RD_1Hz rd_1hz_1 (.EN(and_2_out), .clk(clk), .reset(reset), .output_clk(rd_1hz_1_output_clk));
  RD_05Hz rd_05hz_1 (.EN(and_3_out), .clk(clk), .reset(reset), .output_clk(rd_05hz_1_output_clk));
  RD_025Hz rd_025hz_1 (.EN(and_4_out), .clk(clk), .reset(reset), .output_clk(rd_025hz_1_output_clk));
  Multiplexer #(.enable("false"), .select(2)) multiplexer_1 (
    .in0(and_1_out), .in1(rd_1hz_1_output_clk), .in2(rd_05hz_1_output_clk), .in3(rd_025hz_1_output_clk),
    .out(output_clk), .sel({SW1, SW0}));
endmodule

module RD_1Hz (
  input  EN,
  input  clk,
  input  reset,
  output output_clk
);

  wire and_1_out, and_2_out, and_3_out, t_ff_1_q, t_ff_2_q, t_ff_3_q, t_ff_4_q;

  T_Flip_Flop t_ff_1 (.T(EN), .clk(clk), .Q(t_ff_1_q), .reset(reset));  // open: Qn, preset
  and and_1 (and_1_out, EN, t_ff_1_q);
  T_Flip_Flop t_ff_2 (.T(and_1_out), .clk(clk), .Q(t_ff_2_q), .reset(reset));  // open: Qn, preset
  and and_2 (and_2_out, and_1_out, t_ff_2_q);
  T_Flip_Flop t_ff_3 (.T(and_2_out), .clk(clk), .Q(t_ff_3_q), .reset(reset));  // open: Qn, preset
  and and_3 (and_3_out, and_2_out, t_ff_3_q);
  T_Flip_Flop t_ff_4 (.T(and_3_out), .clk(clk), .Q(t_ff_4_q), .reset(reset));  // open: Qn, preset
  Adder #(.width(1)) adder_1 (.a(t_ff_4_q), .b(1'b1), .out(output_clk));  // open: cin, cout
endmodule

module RD_05Hz (
  input  EN,
  input  clk,
  input  reset,
  output output_clk
);

  wire and_1_out, and_2_out, and_3_out, and_4_out, t_ff_1_q, t_ff_2_q, t_ff_3_q, t_ff_4_q, t_ff_5_q;

  T_Flip_Flop t_ff_1 (.T(EN), .clk(clk), .Q(t_ff_1_q), .reset(reset));  // open: Qn, preset
  and and_1 (and_1_out, EN, t_ff_1_q);
  T_Flip_Flop t_ff_2 (.T(and_1_out), .clk(clk), .Q(t_ff_2_q), .reset(reset));  // open: Qn, preset
  and and_2 (and_2_out, and_1_out, t_ff_2_q);
  T_Flip_Flop t_ff_3 (.T(and_2_out), .clk(clk), .Q(t_ff_3_q), .reset(reset));  // open: Qn, preset
  and and_3 (and_3_out, and_2_out, t_ff_3_q);
  T_Flip_Flop t_ff_4 (.T(and_3_out), .clk(clk), .Q(t_ff_4_q), .reset(reset));  // open: Qn, preset
  and and_4 (and_4_out, and_3_out, t_ff_4_q);
  T_Flip_Flop t_ff_5 (.T(and_4_out), .clk(clk), .Q(t_ff_5_q), .reset(reset));  // open: Qn, preset
  Adder #(.width(1)) adder_1 (.a(t_ff_5_q), .b(1'b1), .out(output_clk));  // open: cin, cout
endmodule

module RD_025Hz (
  input  EN,
  input  clk,
  input  reset,
  output output_clk
);

  wire and_1_out, and_2_out, and_3_out, and_4_out, and_5_out, t_ff_1_q, t_ff_2_q, t_ff_3_q, t_ff_4_q,
       t_ff_5_q, t_ff_6_q;

  T_Flip_Flop t_ff_1 (.T(EN), .clk(clk), .Q(t_ff_1_q), .reset(reset));  // open: Qn, preset
  and and_1 (and_1_out, EN, t_ff_1_q);
  T_Flip_Flop t_ff_2 (.T(and_1_out), .clk(clk), .Q(t_ff_2_q), .reset(reset));  // open: Qn, preset
  and and_2 (and_2_out, and_1_out, t_ff_2_q);
  T_Flip_Flop t_ff_3 (.T(and_2_out), .clk(clk), .Q(t_ff_3_q), .reset(reset));  // open: Qn, preset
  and and_3 (and_3_out, and_2_out, t_ff_3_q);
  T_Flip_Flop t_ff_4 (.T(and_3_out), .clk(clk), .Q(t_ff_4_q), .reset(reset));  // open: Qn, preset
  and and_4 (and_4_out, and_3_out, t_ff_4_q);
  T_Flip_Flop t_ff_5 (.T(and_4_out), .clk(clk), .Q(t_ff_5_q), .reset(reset));  // open: Qn, preset
  and and_5 (and_5_out, and_4_out, t_ff_5_q);
  T_Flip_Flop t_ff_6 (.T(and_5_out), .clk(clk), .Q(t_ff_6_q), .reset(reset));  // open: Qn, preset
  Adder #(.width(1)) adder_1 (.a(t_ff_6_q), .b(1'b1), .out(output_clk));  // open: cin, cout
endmodule

module DisplayCounter (
  input  clear,
  input  clk,
  input  Enable,
  output [3:0] Q
);

  wire and_1_out, not_1_out, or_1_out;

  not not_1 (not_1_out, Enable);
  or or_1 (or_1_out, and_1_out, not_1_out);
  Counter #(.max('hf), .width(4)) counter_1 (
    .clr(clear), .load(or_1_out), .up(1'b1), .clk(clk), .D(4'b0000), .Q(Q));  // open: count, carry
  and and_1 (and_1_out, Q[0], Q[1], Q[2], Q[3]);
endmodule
