// Logisim project lab5_part3.circ as structural Verilog: 2 circuits, main circuit LUT
module LUT (
  input  EN,
  input  reset,
  input  [2:0] letter,
  input  load_n
);

  wire clk_out, or_1_out, rd_1_output_clk;
  wire [14:0] multiplexer_1_out, shift_register_1_out, shifter_1_out;

  Clock clk (.out(clk_out));
  RD rd_1 (.clear(reset), .clk(clk_out), .Enable(EN), .output_clk(rd_1_output_clk));
  Multiplexer #(.enable("false"), .select(3), .width(15)) multiplexer_1 (
    .in0(15'h2a), .in1(15'he), .in2(15'hea), .in3(15'h3aa), .in4(15'h3ba), .in5(15'heae), .in6(15'h3bae),
    .in7(15'haee), .out(multiplexer_1_out), .sel(letter));
  or or_1 (or_1_out, rd_1_output_clk, load_n);
  Shift_Register #(.length(1), .width(15)) shift_register_1 (
    .in(shifter_1_out), .clk(or_1_out), .out(shift_register_1_out), .load(load_n), .clr(reset),
    .d0(multiplexer_1_out));  // open: shift, q0
  LED led_1 (.in(shift_register_1_out[0]));
  Shifter #(.shift("lr"), .width(15)) shifter_1 (.in(shift_register_1_out), .\dist (4'b0001), .out(shifter_1_out));

  // Notes on the sheet:
  //   KEY0
  //   SW[2:0]
  //   LEDR0
endmodule

module RD (
  input  clear,
  input  clk,
  input  Enable,
  output output_clk
);

  wire not_1_out;
  wire [2:0] counter_1_q;

  not not_1 (not_1_out, Enable);
  Counter #(.max('h7), .width(3)) counter_1 (
    .clr(clear), .load(not_1_out), .up(1'b1), .clk(clk), .D(3'b000), .Q(counter_1_q));  // open: count, carry
  and and_1 (output_clk, counter_1_q[0], counter_1_q[1], counter_1_q[2]);
endmodule
