// Logisim project lab7_part1.circ as structural Verilog: 2 circuits, main circuit Part1_32x4_RAM
module main (
  input  WriteEn,
  input  Clock,
  input  OutputEn,
  input  Reset,
  output [3:0] DataOut
);

  wire register_3_q, register_4_q;
  wire [3:0] adder_2_out, register_2_q;
  wire [4:0] adder_1_out, register_1_q;

  Adder #(.width(5)) adder_1 (.a(register_1_q), .b(5'b00001), .out(adder_1_out));  // open: cin, cout
  Adder #(.width(4)) adder_2 (.a(register_2_q), .b(4'b0001), .out(adder_2_out));  // open: cin, cout
  Register #(.width(5)) register_1 (.D(adder_1_out), .clk(Clock), .Q(register_1_q), .clr(Reset));  // open: en
  Register #(.width(4)) register_2 (.D(adder_2_out), .clk(Clock), .Q(register_2_q), .clr(Reset));  // open: en
  Register #(.width(1)) register_3 (.D(WriteEn), .clk(Clock), .Q(register_3_q), .clr(Reset));  // open: en
  Register #(.width(1)) register_4 (.D(OutputEn), .clk(Clock), .Q(register_4_q), .clr(Reset));  // open: en
  RAM #(.addrWidth(5), .dataWidth(4)) ram_1 (
    .addr(register_1_q), .we(register_3_q), .oe(register_4_q), .clk(Clock), .din(register_2_q), .dout(DataOut));
  Hex_Digit_Display hex_digit_display_1 (.value(DataOut));  // open: dp

  // Notes on the sheet:
  //   Address
  //   DataIn
endmodule

module Part1_32x4_RAM (
  input  [4:0] Address,
  input  [3:0] DataIn,
  input  WriteEn,
  input  Clock,
  input  OutputEn,
  input  Reset,
  output [3:0] DataOut
);

  wire register_3_q, register_4_q;
  wire [3:0] register_2_q;
  wire [4:0] register_1_q;

  Register #(.width(5)) register_1 (.D(Address), .clk(Clock), .Q(register_1_q), .clr(Reset));  // open: en
  Register #(.width(4)) register_2 (.D(DataIn), .clk(Clock), .Q(register_2_q), .clr(Reset));  // open: en
  Register #(.width(1)) register_3 (.D(WriteEn), .clk(Clock), .Q(register_3_q), .clr(Reset));  // open: en
  Register #(.width(1)) register_4 (.D(OutputEn), .clk(Clock), .Q(register_4_q), .clr(Reset));  // open: en
  RAM #(.addrWidth(5), .dataWidth(4)) ram_1 (
    .addr(register_1_q), .we(register_3_q), .oe(register_4_q), .clk(Clock), .din(register_2_q), .dout(DataOut));
endmodule
