// Logisim project lab7_part2.circ as structural Verilog: 10 circuits, main circuit main
module main (
  input  Enable,
  input  reset,
  input  [6:0] x,
  input  [6:0] y,
  output [6:0] out_5,
  output [6:0] out_6
);

  wire Clk_out, not_1_out, state_table_1_id_x_add, state_table_1_id_y_add;
  wire [6:0] state_table_1_x_add, state_table_1_y_add;

  Clock Clk (.out(Clk_out));
  not not_1 (not_1_out, Enable);
  state_table state_table_1 (
    .reset(not_1_out), .en(Enable), .clk(Clk_out), .Id_x_add(state_table_1_id_x_add),
    .x_add(state_table_1_x_add), .Id_y_add(state_table_1_id_y_add), .y_add(state_table_1_y_add));
  // RGB_Video rgb_video_1: pin names not known; wires that end beside it: reset, Clk_out, Enable, 24'h73f0, out_5, out_6, 24'h73f0
  datapath datapath_1 (
    .x_coor(x), .Id_x_add(state_table_1_id_x_add), .clk(Clk_out), .reset(reset), .x_add(state_table_1_x_add),
    .y_coor(y), .Id_y_add(state_table_1_id_y_add), .y_add(state_table_1_y_add), .x_coor_out(out_5),
    .y_coor_out(out_6));
endmodule

module datapath (
  input  [6:0] x_coor,
  input  Id_x_add,
  input  clk,
  input  reset,
  input  [6:0] x_add,
  input  [6:0] y_coor,
  input  Id_y_add,
  input  [6:0] y_add,
  output [6:0] x_coor_out,
  output [6:0] y_coor_out
);

  wire [6:0] multiplexer_1_out, multiplexer_2_out, register_1_q, register_2_q, register_3_q, register_4_q;

  Multiplexer #(.enable("false"), .width(7)) multiplexer_1 (
    .in0(x_coor), .in1(x_coor_out), .out(multiplexer_1_out), .sel(Id_x_add));
  Multiplexer #(.enable("false"), .width(7)) multiplexer_2 (
    .in0(y_coor), .in1(y_coor_out), .out(multiplexer_2_out), .sel(Id_y_add));
  Register #(.width(7)) register_1 (.D(multiplexer_1_out), .en(1'b1), .clk(clk), .Q(register_1_q), .clr(reset));
  Register #(.width(7)) register_2 (.D(multiplexer_2_out), .en(1'b1), .clk(clk), .Q(register_2_q), .clr(reset));
  Register #(.width(7)) register_3 (.D(x_add), .clk(clk), .Q(register_3_q), .clr(reset));  // open: en
  Register #(.width(7)) register_4 (.D(y_add), .clk(clk), .Q(register_4_q), .clr(reset));  // open: en
  Adder #(.width(7)) adder_1 (.a(register_1_q), .b(register_3_q), .out(x_coor_out));  // open: cin, cout
  Adder #(.width(7)) adder_2 (.a(register_2_q), .b(register_4_q), .out(y_coor_out));  // open: cin, cout

  // Notes on the sheet:
  //   Id_x
  //   Id_y
endmodule

module state_table (
  input  reset,
  input  en,
  input  clk,
  output Id_x_add,
  output [6:0] x_add,
  output Id_y_add,
  output [6:0] y_add
);

  wire [4:0] state_1_curr_state;

  state state_1 (.clear(reset), .Enable(en), .clk(clk), .curr_state(state_1_curr_state));
  Id_x_add_state_table id_x_add_state_table_1 (.state(state_1_curr_state), .Id_x_add(Id_x_add));
  x_add_state_table x_add_state_table_1 (.state(state_1_curr_state), .x_add(x_add));
  Id_y_add_state_table id_y_add_state_table_1 (.state(state_1_curr_state), .Id_y_add(Id_y_add));
  y_add_state_table y_add_state_table_1 (.state(state_1_curr_state), .y_add(y_add));
endmodule

module state (
  input  clear,
  input  Enable,
  input  clk,
  output [4:0] curr_state
);

  wire and_1_out, counter_2_carry, multiplexer_1_out, multiplexer_2_out, not_1_out, not_2_out, not_3_out,
       not_4_out, not_5_out, not_6_out, or_1_out;
  wire [4:0] adder_1_out, bit_extender_1_out, bit_extender_2_out, counter_1_q, register_1_q;

  not not_1 (not_1_out, Enable);
  or or_1 (or_1_out, not_1_out, counter_2_carry);
  Counter #(.max('h10), .width(5)) counter_1 (
    .clr(clear), .load(or_1_out), .up(1'b1), .clk(clk), .D({5{1'b0}}), .Q(counter_1_q));  // open: count, carry
  not not_2 (not_2_out, counter_1_q[0]);
  not not_3 (not_3_out, counter_1_q[1]);
  not not_4 (not_4_out, counter_1_q[2]);
  not not_5 (not_5_out, counter_1_q[3]);
  not not_6 (not_6_out, counter_1_q[4]);
  Multiplexer #(.enable("false")) multiplexer_1 (.in0(1'b0), .in1(1'b1), .out(multiplexer_1_out), .sel(and_1_out));
  and and_1 (and_1_out, not_2_out, not_3_out, not_4_out, not_5_out, not_6_out);
  assign bit_extender_1_out = {{4{1'b0}}, multiplexer_1_out};  // Bit_Extender bit_extender_1
  Adder #(.width(5)) adder_1 (.a(bit_extender_1_out), .b(counter_1_q), .out(adder_1_out));  // open: cin, cout
  Register #(.width(5)) register_1 (.D(adder_1_out), .clk(clk), .Q(register_1_q), .clr(clear));  // open: en
  Counter #(.max('h10), .width(5)) counter_2 (
    .clr(clear), .clk(and_1_out), .carry(counter_2_carry));  // open: load, up, count, D, Q
  assign bit_extender_2_out = {{4{1'b0}}, multiplexer_2_out};  // Bit_Extender bit_extender_2
  Multiplexer #(.enable("false")) multiplexer_2 (
    .in0(1'b0), .in1(1'b1), .out(multiplexer_2_out), .sel(counter_2_carry));
  Subtractor #(.width(5)) subtractor_1 (.a(bit_extender_2_out), .b(register_1_q), .out(curr_state));  // open: bin, bout
endmodule

module next_state_state_table (
  input  [4:0] state,
  output [4:0] next_state
);

  Adder #(.width(5)) adder_1 (.a(state), .b(5'b00001), .out(next_state));  // open: cin, cout
endmodule

module Id_x_add_state_table (
  input  [4:0] state,
  output Id_x_add
);

  wire and_1_out, nor_1_out, not_1_out, not_2_out, not_3_out, not_4_out, or_1_out;

  not not_1 (not_1_out, state[0]);
  not not_2 (not_2_out, state[1]);
  not not_3 (not_3_out, state[2]);
  not not_4 (not_4_out, state[3]);
  nor nor_1 (nor_1_out, state[0], state[1], state[2], state[3], state[4]);
  and and_1 (and_1_out, not_1_out, not_2_out, not_3_out, not_4_out, state[4]);
  or or_1 (or_1_out, nor_1_out, and_1_out);
  not not_5 (Id_x_add, or_1_out);
endmodule

module x_add_state_table (
  input  [4:0] state,
  output [6:0] x_add
);

  wire and_1_out, nor_1_out, not_1_out, not_2_out, not_3_out, not_4_out, not_5_out, or_1_out;

  not not_1 (not_1_out, state[0]);
  not not_2 (not_2_out, state[1]);
  not not_3 (not_3_out, state[2]);
  not not_4 (not_4_out, state[3]);
  nor nor_1 (nor_1_out, state[0], state[1], state[2], state[3], state[4]);
  and and_1 (and_1_out, not_1_out, not_2_out, not_3_out, not_4_out, state[4]);
  or or_1 (or_1_out, nor_1_out, and_1_out);
  not not_5 (not_5_out, or_1_out);
  assign x_add = {{6{1'b0}}, not_5_out};  // Bit_Extender bit_extender_1
endmodule

module Id_y_state_table (
  input  [4:0] state,
  output Id_y
);

  wire and_1_out, nor_1_out, not_1_out, not_2_out, not_3_out, not_4_out;

  not not_1 (not_1_out, state[0]);
  not not_2 (not_2_out, state[1]);
  not not_3 (not_3_out, state[2]);
  not not_4 (not_4_out, state[3]);
  nor nor_1 (nor_1_out, state[0], state[1], state[2], state[3], state[4]);
  and and_1 (and_1_out, not_1_out, not_2_out, not_3_out, not_4_out, state[4]);
  or or_1 (Id_y, nor_1_out, and_1_out);
endmodule

module Id_y_add_state_table (
  input  [4:0] state,
  output Id_y_add
);

  wire and_1_out, not_1_out, not_2_out, not_3_out, not_4_out, not_5_out;

  not not_1 (not_1_out, state[0]);
  not not_2 (not_2_out, state[1]);
  not not_3 (not_3_out, state[2]);
  not not_4 (not_4_out, state[3]);
  not not_5 (not_5_out, state[4]);
  and and_1 (and_1_out, not_1_out, not_2_out, not_3_out, not_4_out, not_5_out);
  not not_6 (Id_y_add, and_1_out);
endmodule

module y_add_state_table (
  input  [4:0] state,
  output [6:0] y_add
);

  wire and_1_out, not_1_out, not_2_out, not_3_out, not_4_out;

  not not_1 (not_1_out, state[0]);
  not not_2 (not_2_out, state[1]);
  not not_3 (not_3_out, state[2]);
  not not_4 (not_4_out, state[3]);
  and and_1 (and_1_out, not_1_out, not_2_out, not_3_out, not_4_out, state[4]);
  assign y_add = {{6{1'b0}}, and_1_out};  // Bit_Extender bit_extender_1
endmodule
